# Fritzing sketch schema (saved by Fritzing 0.9.3b)
breadboards: 1

parts:
  PIR1 = PIR sensor  # not connected
  PIR2 = PIR sensor
  Raspberry_Pi_1 = Raspberry Pi B rev2
  LED1 = LED - 5mm [color="Red (633nm)" package="5 mm [THT]"]
  R1 = Resistor [tolerance=±5% resistance=220 package=THT]

nets:
  VDD: PIR2.VDD, Raspberry_Pi_1.5V
  N1: PIR2.SIG, Raspberry_Pi_1.GPIO_27
  GND: PIR2.GND, Raspberry_Pi_1.GND, LED1.anode
  N2: Raspberry_Pi_1.GPIO_18, R1.Pin_0
  N3: LED1.cathode, R1.Pin_1
